# Fritzing sketch aic_pico_pn5180 (saved by Fritzing 0.9.3b)

parts:
  元件1 = PN5180-NFC
  Mod1 = Raspberry Pi Pico
  U2 = WS2812 RGB LED strip

nets:
  5V: 元件1.5V, Mod1.pin_39, U2.VCC
  N1: 元件1.3.3V, Mod1.pin_36
  N2: 元件1.RST, Mod1.pin_32
  N3: 元件1.NSS, Mod1.pin_22
  N4: 元件1.MOSI, Mod1.pin_25
  N5: 元件1.MISO, Mod1.pin_21
  N6: 元件1.SCK, Mod1.pin_24
  N7: 元件1.BUSY, Mod1.pin_31
  GND: 元件1.GND, Mod1.pin_28, Mod1.pin_33, Mod1.pin_38, U2.GND
  N8: Mod1.pin_16, U2.DIN

notes:
  Rasp Pi Pico PN5180
  VSYS 5V
  3.3V 3.3V
  GPIO 27 RST
  GPIO 17 NSS
  GPIO 19 MOSI
  GPIO 16 MISO
  GPIO 18 SCK
  GPIO 26 BUSY
  GND GND

custom parts:
  PN5180-NFC: RFID High Frequency IC card reader/writer based on the PN5180 chip from NXP.
  Raspberry Pi Pico: Raspberry Pi Pico. Based around the RP2040 microcontroller the Pico is a low cost microcontroller device bringing Raspberry Pi quality, cost, and easy of use to the microcontroller space. Jan 2021, Split part in to two versions: tht (this one) and SMD. This one will drill holes for a .1 in header in pcb to allow plugging in the module as well as providing pads to solder the module to the top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
  WS2812 RGB LED strip: WS2812 strip
