# Fritzing sketch aic_pico_pn532 (saved by Fritzing 0.9.3b)

parts:
  Mod1 = Raspberry Pi Pico
  元件1 = PN532 Elechouse RFID NFC Module V3
  U1 = WS2812 RGB LED strip

nets:
  N1: Mod1.pin_16, U1.DIN
  N2: Mod1.pin_26, 元件1.SDA
  N3: Mod1.pin_27, 元件1.SCL
  GND: Mod1.pin_28, Mod1.pin_38, Mod1.pin_42, 元件1.GND, U1.GND
  N4: Mod1.pin_36, 元件1.VCC
  N5: Mod1.pin_39, U1.VCC

notes:
  Rasp Pi Pico WS2812B
  GND GND
  GPIO 22 Din
  VSYS VCC
  Rasp Pi Pico PN532
  GND GND
  3.3V VCC
  GPIO 20 SDA
  GPIO 21 SCL

custom parts:
  Raspberry Pi Pico: Raspberry Pi Pico. Based around the RP2040 microcontroller the Pico is a low cost microcontroller device bringing Raspberry Pi quality, cost, and easy of use to the microcontroller space. Jan 2021, Split part in to two versions: tht (this one) and SMD. This one will drill holes for a .1 in header in pcb to allow plugging in the module as well as providing pads to solder the module to the top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
  PN532 Elechouse RFID NFC Module V3: NFC is a popular technology in recent years. We often heard this work while smart phone company such as Samsung or HTC introduces their latest high-end phones. Almost all the high-end phone in the market support NFC. Near field communication (NFC) is a set of standards for smart phones and similar devices to establish radio communication with each other by touching them together or bringing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
  WS2812 RGB LED strip: WS2812 strip
